# Fritzing sketch indecision (saved by Fritzing 1.0.1rc)
breadboards: 1

parts:
  U1 = 555 Timer [package="DIP8 [THT]"]
  DS2Y-5-DC5V1 = DS2Y-5-DC5V [part_number=DS2Y-5-DC5V]
  C1 = Capacitor Polarized [package=cpol-radial-100uf-25v]
  LED1 = smd LED [color="Yellow (585nm)" package="0805 [SMD]"]  # not connected
  LED2 = smd LED [color="Yellow (585nm)" package="0805 [SMD]"]
  R1 = Resistor [tolerance=±5% resistance=220 package="0603 [SMD]"]
  R2 = Resistor [tolerance=±5% resistance=220 package="0603 [SMD]"]  # not connected
  R3 = Trimmer Potentiometer [maximum_resistance=10kΩ knob_status=50% power=0.5W package=THT]

nets:
  N1: U1.Ground, DS2Y-5-DC5V1.8_N.O., C1.-, LED2.cathode
  N2: U1.Trigger, U1.Threshold, C1.+, R3.leg2
  N3: U1.Output, DS2Y-5-DC5V1.9_N.O.
  N4: U1.Reset, U1.Vcc_Supply_Voltage, R3.leg1
  N5: DS2Y-5-DC5V1.16_-, R1.Pin_0

notes:
  Postive 5V
  Ground
